// Logisim project Practica02.circ as structural Verilog: 4 circuits, main circuit main
module main (
  input  A,
  input  B,
  input  A_2,
  input  B_2,
  input  A_3,
  input  B_3,
  input  A_4,
  output Salida,
  output Salida_2,
  output Salida_3,
  output Salida_4
);

  wire pull_resistor_5_node, transistor_2_out, transistor_6_out, transistor_7_out, transistor_9_out;

  Transistor #(.\type ("n")) transistor_1 (.in(transistor_2_out), .out(Salida), .gate(B));
  Transistor #(.\type ("n")) transistor_2 (.in(1'b1), .out(transistor_2_out), .gate(A));
  Transistor #(.\type ("n")) transistor_3 (.in(1'b1), .out(Salida_3), .gate(A_3));
  Transistor #(.\type ("n")) transistor_4 (.in(1'b1), .out(Salida_3), .gate(B_3));
  Transistor transistor_5 (.in(1'b1), .out(Salida_4), .gate(A_4));
  Pull_Resistor pull_resistor_1 (.node(Salida));
  Pull_Resistor pull_resistor_2 (.node(Salida_3));
  Pull_Resistor pull_resistor_3 (.node(Salida_4));
  Transistor transistor_6 (.in(transistor_7_out), .out(transistor_6_out), .gate(A_2));
  Transistor #(.\type ("n")) transistor_7 (.in(1'b1), .out(transistor_7_out), .gate(B_2));
  Pull_Resistor pull_resistor_4 (.node(transistor_6_out));
  Transistor #(.\type ("n")) transistor_8 (.in(1'b1), .out(Salida_2), .gate(transistor_6_out));
  Transistor #(.\type ("n")) transistor_9 (.in(1'b1), .out(transistor_9_out), .gate(A_2));
  Pull_Resistor pull_resistor_5 (.node(pull_resistor_5_node));
  Transistor #(.\type ("n"), .gate("br")) transistor_10 (.in(1'b1), .out(Salida_2), .gate(pull_resistor_5_node));
  Pull_Resistor pull_resistor_6 (.node(Salida_2));
  Transistor transistor_11 (.in(transistor_9_out), .out(pull_resistor_5_node), .gate(B_2));

  // Notes on the sheet:
  //   AND
  //   OR
  //   NOT
  //   Entrada
  //   Entradas
  //   Entradas
  //   Circuitos: Compuertas Logicas
  //   XOR
  //   Entradas
endmodule

module Ejercicio_2 (
  input  p,
  input  q,
  input  r,
  output Salida
);

  wire and_1_out, and_2_out, not_1_out, not_2_out;

  and and_1 (and_1_out, p, not_1_out, r);
  not not_1 (not_1_out, q);
  or or_1 (Salida, and_1_out, and_2_out);
  not not_2 (not_2_out, r);
  and and_2 (and_2_out, p, q, not_2_out);

  // Notes on the sheet:
  //   Llave
  //   Circuito: Puerta Inteligente
  //   Entradas
  //   Switch
  //   Sensor
endmodule

module Ejercicio_3 (
  input  in_1,
  input  in_2,
  input  in_3,
  input  in_4,
  output out_5,
  output x_y,
  output x_y_2
);

  wire and_1_out, and_2_out, and_3_out, and_4_out, and_5_out, and_6_out, and_7_out, and_8_out, and_9_out,
       and_10_out, not_1_out, not_2_out, not_3_out, not_4_out;

  and and_1 (and_1_out, not_1_out, in_3);
  and and_2 (and_2_out, not_1_out, not_2_out, in_4);
  or or_1 (out_5, and_1_out, and_2_out, and_3_out);
  and and_3 (and_3_out, not_2_out, in_3, in_4);
  not not_1 (not_1_out, in_1);
  not not_2 (not_2_out, in_2);
  and and_4 (and_4_out, not_1_out, not_2_out, not_3_out, not_4_out);
  and and_5 (and_5_out, in_1, not_2_out, in_3, not_4_out);
  or or_2 (x_y, and_4_out, and_5_out, and_6_out, and_7_out);
  and and_6 (and_6_out, not_1_out, in_2, not_3_out, in_4);
  not not_3 (not_3_out, in_3);
  and and_7 (and_7_out, in_1, in_2, in_3, in_4);
  not not_4 (not_4_out, in_4);
  and and_8 (and_8_out, in_1, not_3_out);
  and and_9 (and_9_out, in_2, not_3_out, not_4_out);
  or or_3 (x_y_2, and_8_out, and_9_out, and_10_out);
  and and_10 (and_10_out, in_1, in_2, not_4_out);

  // Notes on the sheet:
  //   x<y
  //   X
  //   Circuito: Comparador de 2 bits
  //   Entradas
  //   Salidas
  //   Y
endmodule

module Ejercicio_4 (
  input  A,
  input  B,
  input  C,
  input  D,
  output Salida
);

  wire and_1_out, and_2_out, not_1_out, not_2_out, or_1_out, or_3_out;

  and and_1 (and_1_out, A, or_1_out);
  or or_1 (or_1_out, B, not_1_out, not_2_out);
  or or_2 (Salida, and_1_out, and_2_out);
  not not_1 (not_1_out, C);
  or or_3 (or_3_out, B, not_2_out);
  and and_2 (and_2_out, or_3_out, not_1_out);
  not not_2 (not_2_out, D);

  // Notes on the sheet:
  //   X
  //   Circuito: Tabla de Verdad(X?Y).
  //   Entradas
  //   X ? Y
  //   Y
endmodule
