// Logisim project Practica 4.circ as structural Verilog
module Automata (
  input  Input,
  input  Switch
);

  wire and_1_out, and_2_out, and_3_out, clock_1_out, not_1_out, s_r_ff_1_qn, s_r_ff_2_qn;
  wire [1:0] s_r_ff_2_q;

  not not_1 (not_1_out, Input);
  and and_1 (and_1_out, s_r_ff_1_qn, not_1_out, s_r_ff_2_q[0]);
  and and_2 (and_2_out, s_r_ff_2_q[1], not_1_out, s_r_ff_2_q[0]);
  and and_3 (and_3_out, not_1_out, s_r_ff_2_qn);
  Clock clock_1 (.out(clock_1_out));
  S_R_Flip_Flop s_r_ff_1 (
    .S(and_1_out), .clk(clock_1_out), .R(and_2_out), .Q(s_r_ff_2_q[1]), .Qn(s_r_ff_1_qn));  // open: preset, reset, en
  S_R_Flip_Flop s_r_ff_2 (
    .S(and_3_out), .clk(clock_1_out), .R(s_r_ff_2_q[0]), .Q(s_r_ff_2_q[0]), .Qn(s_r_ff_2_qn));  // open: preset, reset, en
  Hex_Digit_Display hex_digit_display_1 (.value({{2{Switch}}, s_r_ff_2_q}));  // open: dp

  // Notes on the sheet:
  //   Circuito: Automata.
endmodule

module Registro_8_bits (
  input  [7:0] Entrada,
  output [7:0] Salida
);

  wire clock_1_out;

  Clock clock_1 (.out(clock_1_out));
  D_Flip_Flop d_ff_1 (.clk(clock_1_out), .D(Entrada[0]), .Q(Salida[0]));  // open: Qn, preset, en, reset
  D_Flip_Flop d_ff_2 (.clk(clock_1_out), .D(Entrada[1]), .Q(Salida[1]));  // open: Qn, preset, en, reset
  D_Flip_Flop d_ff_3 (.clk(clock_1_out), .D(Entrada[2]), .Q(Salida[2]));  // open: Qn, preset, en, reset
  D_Flip_Flop d_ff_4 (.clk(clock_1_out), .D(Entrada[3]), .Q(Salida[3]));  // open: Qn, preset, en, reset
  D_Flip_Flop d_ff_5 (.clk(clock_1_out), .D(Entrada[4]), .Q(Salida[4]));  // open: Qn, preset, en, reset
  D_Flip_Flop d_ff_6 (.clk(clock_1_out), .D(Entrada[5]), .Q(Salida[5]));  // open: Qn, preset, en, reset
  D_Flip_Flop d_ff_7 (.clk(clock_1_out), .D(Entrada[6]), .Q(Salida[6]));  // open: Qn, preset, en, reset
  D_Flip_Flop d_ff_8 (.clk(clock_1_out), .D(Entrada[7]), .Q(Salida[7]));  // open: Qn, preset, en, reset

  // Notes on the sheet:
  //   Circuito: Registro 8 bits
endmodule

module Shift_Register (
  input  Entrada_en_Serie,
  output out_2,
  output out_3,
  output out_4,
  output out_5,
  output out_6,
  output out_7,
  output out_8,
  output out_9,
  output Salida_en_serie
);

  wire clock_1_out;

  Clock clock_1 (.out(clock_1_out));
  D_Flip_Flop d_ff_1 (.clk(clock_1_out), .D(Entrada_en_Serie), .Q(out_2));  // open: Qn, preset, en, reset
  D_Flip_Flop d_ff_2 (.clk(clock_1_out), .D(out_2), .Q(out_3));  // open: Qn, preset, en, reset
  D_Flip_Flop d_ff_3 (.clk(clock_1_out), .D(out_3), .Q(out_4));  // open: Qn, preset, en, reset
  D_Flip_Flop d_ff_4 (.clk(clock_1_out), .D(out_4), .Q(out_5));  // open: Qn, preset, en, reset
  D_Flip_Flop d_ff_5 (.clk(clock_1_out), .D(out_5), .Q(out_6));  // open: Qn, preset, en, reset
  D_Flip_Flop d_ff_6 (.clk(clock_1_out), .D(out_7), .Q(out_8));  // open: Qn, preset, en, reset
  D_Flip_Flop d_ff_7 (.clk(clock_1_out), .D(out_6), .Q(out_7));  // open: Qn, preset, en, reset
  D_Flip_Flop d_ff_8 (.clk(clock_1_out), .D(out_8), .Q(out_9));  // open: Qn, preset, en, reset

  assign Salida_en_serie = out_9;

  // Notes on the sheet:
  //   Entrada_en_Serie: pull=up
  //   Circuito: Shift Register.
  //   Salidas en Paralelo
endmodule

module Banco_de_Registro (
  input  Escribir,
  input  [1:0] Escribir_Registro,
  input  [1:0] Leer_Registro_1,
  input  [7:0] Escribir_Datos,
  input  [1:0] Leer_Registro_2,
  output [7:0] Leer_Datos_1,
  output [7:0] Leer_Datos_2
);

  wire demultiplexer_2_out0, demultiplexer_2_out1, demultiplexer_2_out2, demultiplexer_2_out3;
  wire [7:0] demultiplexer_1_out0, demultiplexer_1_out1, demultiplexer_1_out2, demultiplexer_1_out3,
       registro_de_8_bits_auxiliar_1_out_3, registro_de_8_bits_auxiliar_2_out_3,
       registro_de_8_bits_auxiliar_3_out_3, registro_de_8_bits_auxiliar_4_out_3;

  Demultiplexer #(.select(2), .width(8), .enable("false")) demultiplexer_1 (
    .out0(demultiplexer_1_out0), .out1(demultiplexer_1_out1), .out2(demultiplexer_1_out2),
    .out3(demultiplexer_1_out3), .in(Escribir_Datos), .sel(Escribir_Registro));
  Registro_de_8_bits_auxiliar registro_de_8_bits_auxiliar_1 (
    .in_2(demultiplexer_1_out0), .in_1(demultiplexer_2_out0), .out_3(registro_de_8_bits_auxiliar_1_out_3));
  Demultiplexer #(.select(2), .enable("false")) demultiplexer_2 (
    .out0(demultiplexer_2_out0), .out1(demultiplexer_2_out1), .out2(demultiplexer_2_out2),
    .out3(demultiplexer_2_out3), .in(Escribir), .sel(Escribir_Registro));
  Registro_de_8_bits_auxiliar registro_de_8_bits_auxiliar_2 (
    .in_2(demultiplexer_1_out1), .in_1(demultiplexer_2_out1), .out_3(registro_de_8_bits_auxiliar_2_out_3));
  Registro_de_8_bits_auxiliar registro_de_8_bits_auxiliar_3 (
    .in_2(demultiplexer_1_out2), .in_1(demultiplexer_2_out2), .out_3(registro_de_8_bits_auxiliar_3_out_3));
  Registro_de_8_bits_auxiliar registro_de_8_bits_auxiliar_4 (
    .in_2(demultiplexer_1_out3), .in_1(demultiplexer_2_out3), .out_3(registro_de_8_bits_auxiliar_4_out_3));
  Multiplexer #(.select(2), .width(8), .enable("false")) multiplexer_1 (
    .in0(registro_de_8_bits_auxiliar_1_out_3), .in1(registro_de_8_bits_auxiliar_2_out_3),
    .in2(registro_de_8_bits_auxiliar_3_out_3), .in3(registro_de_8_bits_auxiliar_4_out_3), .out(Leer_Datos_1),
    .sel(Leer_Registro_1));
  Multiplexer #(.select(2), .width(8), .enable("false")) multiplexer_2 (
    .in0(registro_de_8_bits_auxiliar_1_out_3), .in1(registro_de_8_bits_auxiliar_2_out_3),
    .in2(registro_de_8_bits_auxiliar_3_out_3), .in3(registro_de_8_bits_auxiliar_4_out_3), .out(Leer_Datos_2),
    .sel(Leer_Registro_2));

  // Notes on the sheet:
  //   Circuito: Banco de Registro.
  //   Salidas
endmodule

module Interconexion (
  input  [15:0] Entrada,
  input  Escribir,
  output Acarreo_de_Salida,
  output [7:0] Resultado
);

  wire adder_1_cout, subtractor_1_bout;
  wire [7:0] adder_1_out, banco_de_registro_1_leer_datos_1, banco_de_registro_1_leer_datos_2,
       multiplexer_1_out, subtractor_1_out;

  Banco_de_Registro banco_de_registro_1 (
    .Escribir_Registro(Entrada[13:12]), .Escribir_Datos(Resultado), .Escribir(Escribir),
    .Leer_Registro_1(Entrada[11:10]), .Leer_Registro_2(Entrada[9:8]),
    .Leer_Datos_1(banco_de_registro_1_leer_datos_1), .Leer_Datos_2(banco_de_registro_1_leer_datos_2));
  Multiplexer #(.width(8), .enable("false")) multiplexer_1 (
    .in0(banco_de_registro_1_leer_datos_2), .in1(Entrada[7:0]), .out(multiplexer_1_out), .sel(Entrada[14]));
  Adder adder_1 (
    .a(banco_de_registro_1_leer_datos_1), .b(multiplexer_1_out), .out(adder_1_out), .cout(adder_1_cout));  // open: cin
  Multiplexer #(.width(8), .enable("false")) multiplexer_2 (
    .in0(adder_1_out), .in1(subtractor_1_out), .out(Resultado), .sel(Entrada[15]));
  Subtractor subtractor_1 (
    .a(banco_de_registro_1_leer_datos_1), .b(multiplexer_1_out), .out(subtractor_1_out),
    .bout(subtractor_1_bout));  // open: bin
  Multiplexer #(.enable("false")) multiplexer_3 (
    .in0(adder_1_cout), .in1(subtractor_1_bout), .out(Acarreo_de_Salida), .sel(Entrada[15]));

  // Notes on the sheet:
  //   Circuito: Interconexion
endmodule

module Registro_de_8_bits_auxiliar (
  input  in_1,
  input  [7:0] in_2,
  output [7:0] out_3
);

  D_Flip_Flop d_ff_1 (.clk(in_1), .D(in_2[0]), .Q(out_3[0]));  // open: Qn, preset, en, reset
  D_Flip_Flop d_ff_2 (.clk(in_1), .D(in_2[1]), .Q(out_3[1]));  // open: Qn, preset, en, reset
  D_Flip_Flop d_ff_3 (.clk(in_1), .D(in_2[2]), .Q(out_3[2]));  // open: Qn, preset, en, reset
  D_Flip_Flop d_ff_4 (.clk(in_1), .D(in_2[3]), .Q(out_3[3]));  // open: Qn, preset, en, reset
  D_Flip_Flop d_ff_5 (.clk(in_1), .D(in_2[4]), .Q(out_3[4]));  // open: Qn, preset, en, reset
  D_Flip_Flop d_ff_6 (.clk(in_1), .D(in_2[5]), .Q(out_3[5]));  // open: Qn, preset, en, reset
  D_Flip_Flop d_ff_7 (.clk(in_1), .D(in_2[6]), .Q(out_3[6]));  // open: Qn, preset, en, reset
  D_Flip_Flop d_ff_8 (.clk(in_1), .D(in_2[7]), .Q(out_3[7]));  // open: Qn, preset, en, reset
endmodule
